# Fritzing sketch schematic (saved by Fritzing 0.6.5b)
breadboards: 1

parts:
  LED1 = LED - 5mm [color="Red (633nm)" package="5 mm [THT]"]
  LED2 = LED - 5mm [color="Red (633nm)" package="5 mm [THT]"]
  LED3 = LED - 5mm [color="Red (633nm)" package="5 mm [THT]"]
  LED4 = LED - 5mm [color="Red (633nm)" package="5 mm [THT]"]
  R1 = Resistor [tolerance=±5% resistance=220 package=THT]
  R2 = Resistor [tolerance=±5% resistance=220 package=THT]
  R3 = Resistor [tolerance=±5% resistance=220 package=THT]
  R4 = Resistor [tolerance=±5% resistance=220 package=THT]
  S1 = Pushbutton [package="[THT]"]
  S2 = Pushbutton [package="[THT]"]
  S3 = Pushbutton [package="[THT]"]
  S4 = Pushbutton [package="[THT]"]
  Arduino1 = Arduino

nets:
  N1: LED1.cathode, R2.Pin_0
  N2: LED1.anode, Arduino1.D2
  N3: LED2.cathode, R3.Pin_0
  N4: LED2.anode, Arduino1.D3
  N5: LED3.cathode, R1.Pin_0
  N6: LED3.anode, Arduino1.D4
  N7: LED4.cathode, R4.Pin_0
  N8: LED4.anode, Arduino1.D5
  N9: R1.Pin_1, R2.Pin_1, R3.Pin_1, R4.Pin_1, S1.Pin_3, S1.Pin_4, S2.Pin_3, S2.Pin_4, S3.Pin_3, S3.Pin_4, S4.Pin_3, S4.Pin_4, Arduino1.GND
  N10: S1.Pin_1, S1.Pin_2, Arduino1.D11
  N11: S2.Pin_1, S2.Pin_2, Arduino1.D10
  N12: S3.Pin_1, S3.Pin_2, Arduino1.D9
  N13: S4.Pin_1, S4.Pin_2, Arduino1.D8
